# Fritzing sketch DancingDashSketch (saved by Fritzing 0.9.2b)
breadboards: 1

parts:
  Bauteil1 = Arduino Uno (Rev3)
  Q1 = Basic FET N-Channel [package="TO220 [THT]"]
  R1 = Resistor [tolerance=±5% resistance=10k package=THT]
  S1 = Pushbutton [package="[THT]"]
  D1 = Rectifier Diode [part_number=1N4001 package="300 mil [THT]"]
  M1 = DC Motor
  VCC1 = Battery block 9V

nets:
  N1: Bauteil1.D9_PWM, Q1.gate
  N2: Bauteil1.D2, R1.Pin_1, S1.Pin_3, S1.Pin_4
  N3: Bauteil1.5V, S1.Pin_1, S1.Pin_2
  N4: Bauteil1.GND, Q1.source, R1.Pin_0, VCC1.-
  N5: Q1.drain, D1.cathode, M1.pin_1
  N6: D1.anode, M1.pin_2, VCC1.+

notes:
  Rainbow Dash
